// Logisim project main_file.circ as structural Verilog: 1 circuit, main circuit main
module main (
  input  Ground_Floor,
  input  _1st_floor,
  input  _2nd_floor,
  input  _3rd_floor,
  input  Emergency_Stop,
  output out_6,
  output out_7,
  output out_8
);

  wire clock_1_out, main_2_p5, main_2_p6, main_2_p7, main_2_p8, main_2_p9, main_2_p10, main_2_p11;
  wire [1:0] main_1_p4, priority_encoder_1_out;

  Priority_Encoder #(.select(2)) priority_encoder_1 (
    .in0(Ground_Floor), .in1(_1st_floor), .in2(_2nd_floor), .in3(_3rd_floor), .out(priority_encoder_1_out));  // open: gs, en_out, en_in
  Clock clock_1 (.out(clock_1_out));
  // floor_traversal_main main_1: pin names not known; wires that end beside it: priority_encoder_1_out, Emergency_Stop, clock_1_out, main_1_p4
  // _7_SEGMENT_PRACTICAL3_main main_2: pin names not known; wires that end beside it: 1'b0, 1'b0, main_1_p4[0], main_1_p4[1], main_2_p5, main_2_p6, main_2_p7, main_2_p8, main_2_p9, main_2_p10, main_2_p11
  Comparator #(.width(2), .mode("unsigned")) comparator_1 (
    .a(priority_encoder_1_out), .b(main_1_p4), .gt(out_6), .eq(out_7), .lt(out_8));
  _7_Segment_Display u_7_segment_display_1 (
    .g(main_2_p10), .f(main_2_p5), .a(main_2_p6), .b(main_2_p7), .e(main_2_p9), .d(main_2_p11), .c(main_2_p8));  // open: dp
endmodule
